// Logisim project circuits.circ as structural Verilog: 4 circuits, main circuit myXOR
module myXOR (
  input  x,
  input  in_2,
  input  y
);

  wire and_1_out, and_2_out, not_1_out, not_2_out, or_1_out;

  not not_1 (not_1_out, x);
  not not_2 (not_2_out, y);
  and and_1 (and_1_out, not_1_out, y);
  and and_2 (and_2_out, x, not_2_out);
  or or_1 (or_1_out, and_1_out, and_2_out);
endmodule

module fullAdder (
  input  A,
  input  B,
  input  C,
  output Sum,
  output Carry
);

  wire and_1_out, and_2_out, xor_1_out;

  xor xor_1 (xor_1_out, A, B);
  and and_1 (and_1_out, A, B);
  xor xor_2 (Sum, xor_1_out, C);
  and and_2 (and_2_out, xor_1_out, C);
  or or_1 (Carry, and_2_out, and_1_out);
endmodule

module S_R_Latch (
  input  S,
  input  R,
  output Not_Q,
  output Q
);

  nor nor_1 (Not_Q, S, Q);
  nor nor_2 (Q, Not_Q, R);
endmodule

module D_Latch (
  input  D,
  input  Strobe,
  output Not_Q,
  output Q
);

  wire and_1_out, and_2_out, not_1_out;

  not not_1 (not_1_out, D);
  and and_1 (and_1_out, D, Strobe);
  and and_2 (and_2_out, not_1_out, Strobe);
  S_R_Latch s_r_latch_1 (.S(and_1_out), .R(and_2_out), .Not_Q(Not_Q), .Q(Q));
endmodule
